# Fritzing sketch power_3v3 (saved by Fritzing 0.8.3b)
stripboards: 1

parts:
  U1 = MCP1702 Voltage Regulator [package="TO92 [THT]"]
  C1 = Ceramic Capacitor [capacitance=1µF package="100 mil [THT, multilayer]"]
  C2 = Ceramic Capacitor [capacitance=1µF package="100 mil [THT, multilayer]"]
  J1 = male pin header, 2 pins [form="♂ (male)"]
  J2 = male pin header, 2 pins [form="♂ (male)"]
  J3 = male pin header, 2 pins [form="♂ (male)"]
  J4 = male pin header, 2 pins [form="♂ (male)"]
  J5 = female pin header, 2 pins [form="♀ (female)"]
  J6 = female pin header, 2 pins [form="♀ (female)"]
  J7 = female pin header, 2 pins [form="♀ (female)"]
  J8 = female pin header, 2 pins [form="♀ (female)"]

nets:
  GND: U1.GND, C1.0, C2.0, J1.pin1, J2.pin1, J3.pin1, J4.pin1, J5.pin2, J6.pin2, J7.pin2, J8.pin2
  5V0: U1.Vin, C1.1, J1.pin2, J4.pin2, J5.pin1, J6.pin1
  3V3: U1.Vout, C2.1, J2.pin2, J3.pin2, J7.pin1, J8.pin1

notes:
  NOTE: Use MCP1700-3V3
  Clixx.IO Tabs, 3.3V Power Regulator, 1A

custom parts:
  MCP1702 Voltage Regulator: A MCP1702 Low Dropout Fixed Voltage Regulator (available in 1.2V, 1.5V, 1.8V, 2.5V, 2.8V, 3.0V, 3.3V, 4.0V, 5.0V)
