# Fritzing sketch SingleTab (saved by Fritzing 0.8.3b)
stripboards: 1

parts:
  J1 = male pin header, 2 pins [form="♂ (male)"]
  J2 = male pin header, 2 pins [form="♂ (male)"]

nets:
  -/GND: J1.pin1
  +: J1.pin2
  O: J2.pin1
  I: J2.pin2

notes:
  +
  -
  I
  O
