# Fritzing sketch TwinTab (saved by Fritzing 0.8.7b)
stripboards: 1

parts:
  J1 = male pin header, 5 pins [form="♂ (male)"]
  part = male pin header, 5 pins [form="♂ (male)"]  # not connected

nets:
  GND: J1.pin1
  VCC: J1.pin2
  Extra: J1.pin3
  In: J1.pin4
  Out: J1.pin5

notes:
  -
  +
  *
  I
  O
