# Fritzing sketch 00_Sample (saved by Fritzing 0.8.7b)
circuit board: 4.064cm x 4.953cm
stripboards: 1

parts:
  J1 = male pin header, 5 pins [form="♂ (male)"]
  S1 = Pushbutton [package="[THT]"]
  LED1 = LED - 5mm [color="Red (633nm)" package="5 mm [THT]"]
  R1 = Resistor [tolerance=±5% resistance=330 package=THT]
  R2 = Resistor [tolerance=±5% resistance=1.5k package=THT]
  part = Resistor [tolerance=±5% resistance=220 package=THT]  # not connected

nets:
  GND: J1.pin1, S1.Pin_1, S1.Pin_2, LED1.cathode
  VCC: J1.pin2, R2.Pin_0
  Extra: J1.pin3
  In: J1.pin4, R1.Pin_1
  Out: J1.pin5, S1.Pin_3, S1.Pin_4, R2.Pin_1
  N1: LED1.anode, R1.Pin_0

notes:
  http://thegaragelab.com
  -
  +
  *
  I
  O
