# Fritzing sketch 02_MCP23008 (saved by Fritzing 0.8.3b)
circuit board: 4.064cm x 4.953cm
stripboards: 1

parts:
  J1 = male pin header, 5 pins [form="♂ (male)"]
  IC1 = MCP23008 [package=DIL]
  R1 = Resistor [tolerance=±5% resistance=10k package=THT]
  R2 = Resistor [tolerance=±5% resistance=10k package=THT]
  R3 = Resistor [tolerance=±5% resistance=10k package=THT]
  J2 = double row male pin header, 6 pins [form="♂ (male)"]
  R4 = Resistor [tolerance=±5% resistance=10k package=THT]
  J3 = female pin header, 10 pins [form="♀ (female)"]

nets:
  GND: J1.pin1, IC1.Vss, J2.pin1, J2.pin2, J2.pin3, J3.pin10
  VCC: J1.pin2, IC1.Vdd, R1.Pin_0, R2.Pin_0, R3.Pin_0, R4.Pin_0, J3.pin1
  Extra: J1.pin3, IC1.INT
  In: J1.pin4, IC1.SDA
  Out: J1.pin5, IC1.SCL
  N1: IC1.A2, R1.Pin_1, J2.pin4
  N2: IC1.A1, R2.Pin_1, J2.pin5
  N3: IC1.A0, R3.Pin_1, J2.pin6
  N4: IC1.RESET, R4.Pin_1
  N5: IC1.GP0, J3.pin9
  N6: IC1.GP1, J3.pin8
  N7: IC1.GP2, J3.pin7
  N8: IC1.GP3, J3.pin6
  N9: IC1.GP4, J3.pin5
  N10: IC1.GP5, J3.pin4
  N11: IC1.GP6, J3.pin3
  N12: IC1.GP7, J3.pin2

notes:
  -
  +
  *
  I
  O
  http://thegaragelab.com, I2C 8 Bit IO Epander Board, 1B
