# Fritzing sketch 02_LPC810 (saved by Fritzing 0.8.3b)
circuit board: 4.064cm x 4.953cm
stripboards: 1

parts:
  CLIXXIO = male pin header, 5 pins [form="♂ (male)"]
  IC1 = LPC810 [package=DIL]
  FTDI = FTDI [package=SIL]
  PWR = male alternating pin header, 2 pins [form="♂ (male)"]
  PGM = male pin header, 2 pins [form="♂ (male)"]
  IO_PORT = male pin header, 6 pins [form="♂ (male)"]

nets:
  GND: CLIXXIO.pin1, IC1.GND, FTDI.GND/Black, PGM.pin2, IO_PORT.pin6
  VCC: CLIXXIO.pin2, IC1.VCC, PWR.pin1, IO_PORT.pin5
  Extra: CLIXXIO.pin3, IC1.D5/RESET, IO_PORT.pin1
  In: CLIXXIO.pin4, IC1.D1/ISP_EN, PGM.pin1
  Out: CLIXXIO.pin5, IC1.D2
  N1: IC1.D4/ISP_TX, FTDI.RX, IO_PORT.pin2
  N2: IC1.D3, IO_PORT.pin3
  N3: IC1.D0/ISP_RX, FTDI.TX, IO_PORT.pin4
  N4: FTDI.VCC, PWR.pin2

notes:
  -
  +
  *
  I
  O
  http://thegaragelab.com
  LPC810 TwinTab
  http://thegaraglab.com, LPC810 SmartTab, 1A
