# Fritzing sketch 04_PIC16F1827 (saved by Fritzing 0.8.3b)
circuit board: 4.064cm x 4.953cm
stripboards: 1

parts:
  J1 = male pin header, 5 pins [form="♂ (male)"]
  PSEL/RESET = male pin header, 5 pins [form="♂ (male)"]
  FTDI = FTDI [package=SIL]
  PIC16F1827 = 16F1827 [package=DIL]
  GPIO = male pin header, 12 pins [form="♂ (male)"]
  R1 = Resistor [tolerance=±5% resistance=2.2k package=THT]
  R2 = Resistor [tolerance=±5% resistance=2.2k package=THT]

nets:
  GND: J1.pin1, PSEL/RESET.pin1, FTDI.GND/Black, PIC16F1827.VSS, GPIO.pin1
  VCC: J1.pin2, PSEL/RESET.pin3, R1.Pin_1, R2.Pin_1
  Extra: J1.pin3, PIC16F1827.RB3
  In: J1.pin4, PIC16F1827.RB1, R1.Pin_0
  Out: J1.pin5, PIC16F1827.RB4, R2.Pin_0
  RESET: PSEL/RESET.pin2, PIC16F1827.RB6
  PWR: PSEL/RESET.pin4, PIC16F1827.VDD, GPIO.pin2
  N1: PSEL/RESET.pin5, FTDI.VCC
  N2: FTDI.TX, PIC16F1827.RB2
  N3: FTDI.RX, PIC16F1827.RB5
  N4: PIC16F1827.RA2, GPIO.pin10
  N5: PIC16F1827.RA3, GPIO.pin9
  N6: PIC16F1827.RA4, GPIO.pin8
  N7: PIC16F1827.RB0, GPIO.pin4
  N8: PIC16F1827.RB7, GPIO.pin7
  N9: PIC16F1827.RA6, GPIO.pin6
  N10: PIC16F1827.RA7, GPIO.pin5
  N11: PIC16F1827.RA0, GPIO.pin12
  N12: PIC16F1827.RA1, GPIO.pin11

notes:
  -
  +
  *
  I
  O
  http://thegaragelab.com
  http://thegaragelab.com, PIC16F1827 SmartTab, 1B
