# Fritzing sketch 05_Keypad_A (saved by Fritzing 0.8.5b)
circuit board: 4.064cm x 4.953cm
stripboards: 1

parts:
  J1 = male pin header, 5 pins [form="♂ (male)"]
  KEY_UP = PB [package=PBF]
  KEY_FIRE = PB [package=PBF]
  KEY_LEFT = PB [package=PBF]
  KEY_DOWN = PB [package=PBF]
  KEY_RIGHT = PB [package=PBF]
  R10 = Resistor [tolerance=±5% resistance=1M package=THT]
  R11 = Resistor [tolerance=±5% resistance=1k package=THT]
  R12 = Resistor [tolerance=±5% resistance=1k package=THT]
  R13 = Resistor [tolerance=±5% resistance=1k package=THT]
  R14 = Resistor [tolerance=±5% resistance=1k package=THT]
  R15 = Resistor [tolerance=±5% resistance=1k package=THT]
  R16 = Resistor [tolerance=±5% resistance=1k package=THT]

nets:
  GND: J1.pin1, R10.Pin_0, R16.Pin_1
  VCC: J1.pin2, R11.Pin_0
  Extra: J1.pin3
  In: J1.pin4
  Out: J1.pin5, KEY_UP.C, KEY_UP.D, KEY_FIRE.C, KEY_FIRE.D, KEY_LEFT.C, KEY_LEFT.D, KEY_DOWN.C, KEY_DOWN.D, KEY_RIGHT.C, KEY_RIGHT.D, R10.Pin_1
  N1: KEY_UP.A, KEY_UP.B, R15.Pin_1, R16.Pin_0
  N2: KEY_FIRE.A, KEY_FIRE.B, R11.Pin_1, R12.Pin_0
  N3: KEY_LEFT.A, KEY_LEFT.B, R12.Pin_1, R13.Pin_0
  N4: KEY_DOWN.A, KEY_DOWN.B, R13.Pin_1, R14.Pin_0
  N5: KEY_RIGHT.A, KEY_RIGHT.B, R14.Pin_1, R15.Pin_0

notes:
  -
  +
  *
  I
  O
